# Fritzing sketch schematic (saved by Fritzing 0.9.3b)
perfboards: 1

parts:
  U1 = 74HC595 [package="DIP16 [THT]"]
  Part1 = Arduino Uno (Rev3)
  7_Segment1 = 7 Segment Display
  7_Segment2 = 7 Segment Display
  Q1 = NPN-Transistor [package="TO92 [THT]"]
  R1 = Resistor [tolerance=±5% resistance=2.2k package=THT]
  R2 = Resistor [tolerance=±5% resistance=2.2k package=THT]
  Q2 = NPN-Transistor [package="TO92 [THT]"]
  R3 = Resistor [tolerance=±5% resistance=470 package=THT]
  R4 = Resistor [tolerance=±5% resistance=470 package=THT]
  R5 = Resistor [tolerance=±5% resistance=470 package=THT]
  R6 = Resistor [tolerance=±5% resistance=470 package=THT]
  R7 = Resistor [tolerance=±5% resistance=470 package=THT]
  R8 = Resistor [tolerance=±5% resistance=470 package=THT]
  R9 = Resistor [tolerance=±5% resistance=470 package=THT]
  R10 = Resistor [tolerance=±5% resistance=470 package=THT]
  D1 = LED_BARGRAPH_10 [package=led_bargaph_10]
  R11 = Resistor [tolerance=±5% resistance=470 package=THT]
  R12 = Resistor [tolerance=±5% resistance=470 package=THT]
  R13 = Resistor [tolerance=±5% resistance=470 package=THT]
  R14 = Resistor [tolerance=±5% resistance=470 package=THT]
  R15 = Resistor [tolerance=±5% resistance=470 package=THT]
  R16 = Resistor [tolerance=±5% resistance=470 package=THT]
  R17 = Resistor [tolerance=±5% resistance=470 package=THT]
  R18 = Resistor [tolerance=±5% resistance=470 package=THT]
  R19 = Resistor [tolerance=±5% resistance=470 package=THT]
  R20 = Resistor [tolerance=±5% resistance=470 package=THT]
  U2 = 74HC595 [package="DIP16 [THT]"]
  U3 = 74HC595 [package="DIP16 [THT]"]
  R21 = Rotary Potentiometer (Small) [maximum_resistance=10kΩ package=THT]
  S1 = Pushbutton [package="[THT]"]
  LED1 = LED - 5mm [color="Red (633nm)" package="5 mm [THT]"]
  R22 = Resistor [tolerance=±5% resistance=470 package=THT]

nets:
  N1: U1.Q1, R4.Pin_1
  N2: U1.Q2, R5.Pin_1
  N3: U1.Q3, R6.Pin_1
  N4: U1.Q4, R7.Pin_1
  N5: U1.Q5, R8.Pin_1
  N6: U1.Q6, R9.Pin_1
  N7: U1.Q7, R10.Pin_1
  GND: U1.GND, U1.OE, Part1.GND, Q1.E, Q2.E, D1.J_C, D1.I_C, D1.H_C, D1.G_C, D1.F_C, D1.E_C, D1.D_C, D1.C_C, D1.B_C, D1.A_C, U2.GND, U2.OE, U3.GND, U3.OE, R21.leg2, S1.Pin_1, S1.Pin_2, LED1.cathode
  N8: U1.Q7', U2.DS
  VCC: U1.MR, U1.VCC, Part1.5V, U2.MR, U2.VCC, U3.MR, U3.VCC, R21.leg1
  N9: U1.SH_CP, Part1.D4, U2.SH_CP, U3.SH_CP
  N10: U1.ST_CP, Part1.D6_PWM, U2.ST_CP, U3.ST_CP
  N11: U1.DS, Part1.D5_PWM
  N12: U1.Q0, R3.Pin_1
  N13: Part1.A0, R21.wiper
  N14: Part1.A1, S1.Pin_3, S1.Pin_4
  N15: Part1.D2, R1.Pin_0
  N16: Part1.D3_PWM, R2.Pin_0
  N17: 7_Segment1.Segment_A#1, 7_Segment2.Segment_A#1, R4.Pin_0
  N18: 7_Segment1.Segment_F, 7_Segment2.Segment_F, R5.Pin_0
  N19: 7_Segment1.common_cathode, Q1.C
  N20: 7_Segment1.Segment_E, 7_Segment2.Segment_E, R6.Pin_0
  N21: 7_Segment1.Segment_D, 7_Segment2.Segment_D, R7.Pin_0
  N22: 7_Segment1.Segment_DP, 7_Segment2.Segment_DP, R3.Pin_0
  N23: 7_Segment1.Segment_C, 7_Segment2.Segment_C, R8.Pin_0
  N24: 7_Segment1.Segment_B, 7_Segment2.Segment_B, R9.Pin_0
  N25: 7_Segment1.Segment_A#10, 7_Segment2.Segment_A#10, R10.Pin_0
  N26: 7_Segment2.common_cathode, Q2.C
  N27: Q1.B, R1.Pin_1
  N28: R2.Pin_1, Q2.B
  N29: D1.A_A, R11.Pin_1
  N30: D1.B_A, R12.Pin_1
  N31: D1.C_A, R13.Pin_1
  N32: D1.D_A, R14.Pin_1
  N33: D1.E_A, R15.Pin_1
  N34: D1.F_A, R16.Pin_1
  N35: D1.G_A, R17.Pin_1
  N36: D1.H_A, R18.Pin_1
  N37: D1.I_A, R19.Pin_1
  N38: D1.J_A, R20.Pin_1
  N39: R11.Pin_0, U2.Q0
  N40: R12.Pin_0, U2.Q1
  N41: R13.Pin_0, U2.Q2
  N42: R14.Pin_0, U2.Q3
  N43: R15.Pin_0, U2.Q4
  N44: R16.Pin_0, U2.Q5
  N45: R17.Pin_0, U2.Q6
  N46: R18.Pin_0, U2.Q7
  N47: R19.Pin_0, U3.Q0
  N48: R20.Pin_0, U3.Q1
  N49: U2.Q7', U3.DS
  N50: U3.Q2, R22.Pin_0
  N51: LED1.anode, R22.Pin_1
