# Fritzing sketch sensors (saved by Fritzing 0.9.3b)
breadboards: 1

parts:
  Part3 = Adafruit TSL2561 [part_number="Adafruit #439"]
  Part3_2 = MQ-7 breakout
  Part4 = ESP-WROOM-32 [ESP-32S] Module [part_number=ESP-WROOM-32]
  DHT1 = DHT22 Humidity and Temperature Sensor
  R1 = Resistor [tolerance=±5% resistance=10k package=THT]
  Power_plug1 = Power plug [part_number=5V]
  C1 = Electrolytic Capacitor [capacitance=10µF package="100 mil [THT, electrolytic]"]

nets:
  VCC: Part3.VIN, Part3_2.VCC, Part4.RST, DHT1.VDD, R1.Pin_0, Power_plug1.VCC, C1.+
  GND: Part3.GND, Part3_2.GND, Part4.GND, DHT1.GND, Power_plug1.GND, C1.-
  N1: Part3.SDA, Part4.IO17
  N2: Part3.SCL, Part4.IO16
  N3: Part3_2.AO, Part4.IO15
  N4: Part4.IO4, DHT1.DATA, R1.Pin_1

notes:
  5V!

custom parts:
  Adafruit TSL2561: The TSL2561 luminosity sensor is an advanced digital light sensor, ideal for use in a wide range of light situations. Compared to low cost CdS cells, this sensor is more precise, allowing for exact lux calculations and can be configured for different gain/timing ranges to detect light ranges from up to 0.1 - 40,000+ Lux on the fly. The best part of this sensor is that it contains both infrared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
  MQ-7 breakout: SKU: 101282
  ESP-WROOM-32 [ESP-32S] Module: Espressif ESP-WROOM-32 WiFi/Bluetooth LE microcontroller module also known as the Ai-Thinker ESP-32S module with similar formfactor. The ESP32 is a microcontroller chip with WiFi and BLE capabilities. The chip is developed by Espressif and is the successor to the popular ESP8266 WiFi module.
